// Logisim project labo_uart_etu.circ as structural Verilog: 7 circuits, main circuit MAXV_UART
module MAXV_UART (
  input  [7:0] switch_i,
  input  send_i,
  input  clk_i,
  input  nReset_i,
  output [1:0] conf_MAX10_o,
  output TX_done_o
);

  wire not_1_out;
  wire [3:0] Leds_select_i_sw1;
  wire [29:29] tx_uart_serial_tx_o;

  DipSwitch Leds_select_i (
    .sw1(Leds_select_i_sw1[0]), .sw2(Leds_select_i_sw1[1]), .sw3(Leds_select_i_sw1[2]),
    .sw4(Leds_select_i_sw1[3]));  // open: sw5, sw6, sw7, sw8
  not not_1 (not_1_out, nReset_i);
  uart_tx tx_uart (
    .data_i({Leds_select_i_sw1, 8'h55, switch_i}), .send_i(send_i), .clk_i(clk_i), .reset_i(not_1_out),
    .serial_tx_o(tx_uart_serial_tx_o[29]), .tx_done_o(TX_done_o));
  // PortIO #(.number(78)) Con_80p_io: pin names not known; wires that end beside it: {2'b00, tx_uart_serial_tx_o[29], {29{1'b0}}}, {32{1'b0}}, {6'b010000, conf_MAX10_o, {6{1'b0}}}

  // Notes on the sheet:
  //   Attention, votre version de Logisim
  //   ne contient pas de tracker. Si vous
  //   enregistrez votre projet, toutes les
  //   informations du tracker seront
  //   définitivement effacées.
  //   Configuration MAX10 en mode UART
  //   0 = Config non-reconnue
  //   1 = Config connue
  //   Sortie de la config de la MAX10 sur 2 LEDs.
endmodule

module uart_tx (
  input  [19:0] data_i,
  input  send_i,
  input  clk_i,
  input  reset_i,
  output serial_tx_o,
  output tx_done_o
);

  wire comparator_1_eq, load, shift, timer;
  wire [23:0] data;

  Comparator #(.width(24)) comparator_1 (.a(data), .b(24'h800000), .eq(comparator_1_eq));  // open: gt, lt
  timer_12b u_Timer (.value_i(12'h1), .clk_i(clk_i), .load_i(load), .en_i(1'b1), .reset_i(reset_i), .done_o(timer));
  shift_reg_24b Shift_reg (
    .ser_r_i(1'b0), .ser_l_i(1'b0), .value_load_i({1'b0, data_i, 3'b111}), .mode_i({shift, load}),
    .clk_i(clk_i), .reset_i(reset_i), .val_o(data));
  MSS MSS_Control (
    .done_in(comparator_1_eq), .timer_in(timer), .begin_in(send_i), .reset_in(reset_i), .clk(clk_i),
    .mode0_out(load), .mode1_out(shift), .tx_done_out(tx_done_o));
  Multiplexer #(.enable("false")) multiplexer_1 (.in0(data[23]), .in1(1'b1), .out(serial_tx_o), .sel(tx_done_o));

  // Other names for the same wires on the sheet: Clk = clk_i

  // Notes on the sheet:
  //   Attention, votre version de Logisim
  //   ne contient pas de tracker. Si vous
  //   enregistrez votre projet, toutes les
  //   informations du tracker seront
  //   définitivement effacées.
  //   constantes à 1 = bits de stop & bit de parité, constante à 0 = bit de start
  //   Détection du dernier bit de stop
endmodule

module shift_reg_4b (
  input  ser_r_i,
  input  ser_l_i,
  input  [1:0] mode_i,
  input  clk_i,
  input  reset_i,
  input  [3:0] value_load_i,
  output [3:0] val_o
);

  wire multiplexer_1_out, multiplexer_2_out, multiplexer_3_out, multiplexer_4_out;

  Multiplexer #(.select(2), .enable("false")) multiplexer_1 (
    .in0(val_o[3]), .in1(value_load_i[3]), .in2(val_o[2]), .in3(ser_r_i), .out(multiplexer_1_out),
    .sel(mode_i));
  D_Flip_Flop d_ff_1 (.D(multiplexer_1_out), .clk(clk_i), .Q(val_o[3]), .preset(1'b0), .reset(reset_i));  // open: Qn
  Multiplexer #(.select(2), .enable("false")) multiplexer_2 (
    .in0(val_o[2]), .in1(value_load_i[2]), .in2(val_o[1]), .in3(val_o[3]), .out(multiplexer_2_out),
    .sel(mode_i));
  D_Flip_Flop d_ff_2 (.D(multiplexer_2_out), .clk(clk_i), .Q(val_o[2]), .preset(1'b0), .reset(reset_i));  // open: Qn
  Multiplexer #(.select(2), .enable("false")) multiplexer_3 (
    .in0(val_o[1]), .in1(value_load_i[1]), .in2(val_o[0]), .in3(val_o[2]), .out(multiplexer_3_out),
    .sel(mode_i));
  D_Flip_Flop d_ff_3 (.D(multiplexer_3_out), .clk(clk_i), .Q(val_o[1]), .preset(1'b0), .reset(reset_i));  // open: Qn
  Multiplexer #(.select(2), .enable("false")) multiplexer_4 (
    .in0(val_o[0]), .in1(value_load_i[0]), .in2(ser_l_i), .in3(val_o[1]), .out(multiplexer_4_out),
    .sel(mode_i));
  D_Flip_Flop d_ff_4 (.D(multiplexer_4_out), .clk(clk_i), .Q(val_o[0]), .preset(1'b0), .reset(reset_i));  // open: Qn

  // Other names for the same wires on the sheet: L = ser_l_i; R = ser_r_i; Q0 = val_o[0]; Q1 = val_o[1];
  //   Q2 = val_o[2]; Q3 = val_o[3]; D0 = value_load_i[0]; D1 = value_load_i[1]; D2 = value_load_i[2];
  //   D3 = value_load_i[3]

  // Notes on the sheet:
  //   Attention, votre version de Logisim
  //   ne contient pas de tracker. Si vous
  //   enregistrez votre projet, toutes les
  //   informations du tracker seront
  //   définitivement effacées.
endmodule

module shift_reg_24b (
  input  ser_r_i,
  input  ser_l_i,
  input  [23:0] value_load_i,
  input  [1:0] mode_i,
  input  clk_i,
  input  reset_i,
  output [23:0] val_o
);

  shift_reg_8b Reg_LSB (
    .ser_r_i(val_o[8]), .ser_l_i(ser_l_i), .load_i(value_load_i[7:0]), .mod_i(mode_i), .clk_i(clk_i),
    .reset_i(reset_i), .val_o(val_o[7:0]));
  shift_reg_8b Reg_Mid (
    .ser_r_i(val_o[16]), .ser_l_i(val_o[7]), .load_i(value_load_i[15:8]), .mod_i(mode_i), .clk_i(clk_i),
    .reset_i(reset_i), .val_o(val_o[15:8]));
  shift_reg_8b Reg_MSB (
    .ser_r_i(ser_r_i), .ser_l_i(val_o[15]), .load_i(value_load_i[23:16]), .mod_i(mode_i), .clk_i(clk_i),
    .reset_i(reset_i), .val_o(val_o[23:16]));

  // Other names for the same wires on the sheet: Clk = clk_i; Mod_i[1:0] = mode_i; Reset = reset_i; Ser_L = ser_l_i;
  //   Ser_R = ser_r_i; B7_LSB = val_o[7]; B0_Mid = val_o[8]; B7_Mid = val_o[15]; B0_MSB = val_o[16];
  //   Load_0_7[7:0] = value_load_i[7:0]; Load_8_15[7:0] = value_load_i[15:8]; Load_16_23[7:0] = value_load_i[23:16]

  // Notes on the sheet:
  //   Attention, votre version de Logisim
  //   ne contient pas de tracker. Si vous
  //   enregistrez votre projet, toutes les
  //   informations du tracker seront
  //   définitivement effacées.
endmodule

module timer_12b (
  input  [11:0] value_i,
  input  clk_i,
  input  load_i,
  input  en_i,
  input  reset_i,
  output done_o
);

  wire and_1_out, and_2_out, or_1_out;
  wire [11:0] multiplexer_1_out, register_1_q, subtractor_1_out;

  Subtractor #(.width(12)) subtractor_1 (
    .a(register_1_q), .b(12'h1), .out(subtractor_1_out), .bin(1'b0));  // open: bout
  and and_1 (and_1_out, load_i, en_i);
  and and_2 (and_2_out, en_i, ~done_o);  // AND_Gate
  Register #(.width(12)) register_1 (
    .D(multiplexer_1_out), .en(or_1_out), .clk(clk_i), .Q(register_1_q), .clr(reset_i));
  Multiplexer #(.width(12), .enable("false")) multiplexer_1 (
    .in0(subtractor_1_out), .in1(value_i), .out(multiplexer_1_out), .sel(load_i));
  or or_1 (or_1_out, and_1_out, and_2_out);
  Comparator #(.width(12)) comparator_1 (.a(register_1_q), .b({12{1'b0}}), .eq(done_o));  // open: gt, lt

  // Notes on the sheet:
  //   Attention, votre version de Logisim
  //   ne contient pas de tracker. Si vous
  //   enregistrez votre projet, toutes les
  //   informations du tracker seront
  //   définitivement effacées.
endmodule

module shift_reg_8b (
  input  ser_r_i,
  input  ser_l_i,
  input  [7:0] load_i,
  input  [1:0] mod_i,
  input  clk_i,
  input  reset_i,
  output [7:0] val_o
);

  shift_reg_4b shift_reg_lsb (
    .ser_r_i(val_o[4]), .ser_l_i(ser_l_i), .mode_i(mod_i), .clk_i(clk_i), .reset_i(reset_i),
    .value_load_i(load_i[3:0]), .val_o(val_o[3:0]));
  shift_reg_4b shift_reg_msb (
    .ser_r_i(ser_r_i), .ser_l_i(val_o[3]), .mode_i(mod_i), .clk_i(clk_i), .reset_i(reset_i),
    .value_load_i(load_i[7:4]), .val_o(val_o[7:4]));

  // Other names for the same wires on the sheet: load_30[3:0] = load_i[3:0]; load_47[3:0] = load_i[7:4]; SL = ser_l_i;
  //   SR = ser_r_i; B3_LSB = val_o[3]; B1_MSB = val_o[4]

  // Notes on the sheet:
  //   Attention, votre version de Logisim
  //   ne contient pas de tracker. Si vous
  //   enregistrez votre projet, toutes les
  //   informations du tracker seront
  //   définitivement effacées.
endmodule

module MSS (
  input  done_in,
  input  timer_in,
  input  begin_in,
  input  reset_in,
  input  clk,
  output mode0_out,
  output mode1_out,
  output tx_done_out
);

  wire and_1_out, and_2_out, and_3_out, and_4_out, and_5_out, and_6_out, and_7_out, d_ff_1_q, d_ff_2_qn,
       not_1_out, or_1_out, or_2_out, or_3_out, or_4_out, Reset, Swait, Swait_q, Swait_timer;

  D_Flip_Flop d_ff_1 (.D(begin_in), .clk(clk), .Q(d_ff_1_q), .preset(1'b0), .reset(Reset));  // open: Qn
  D_Flip_Flop d_ff_2 (.D(d_ff_1_q), .clk(clk), .Qn(d_ff_2_qn), .preset(1'b0), .reset(Reset));  // open: Q
  and and_1 (and_1_out, d_ff_1_q, d_ff_2_qn);
  and and_2 (and_2_out, timer_in, ~done_in, Swait_timer);  // AND_Gate
  and and_3 (and_3_out, Swait_timer, ~timer_in);  // AND_Gate
  or or_1 (or_1_out, and_3_out, mode1_out);
  or or_2 (or_2_out, Swait_timer, mode1_out);
  and and_4 (and_4_out, or_2_out, done_in);
  and and_5 (and_5_out, Swait, ~and_1_out);  // AND_Gate
  and and_6 (and_6_out, and_1_out, Swait);
  or or_3 (or_3_out, mode0_out, and_2_out);
  and and_7 (and_7_out, ~done_in, or_1_out);  // AND_Gate
  or or_4 (or_4_out, and_4_out, and_5_out);
  D_Flip_Flop u_Swait (.D(not_1_out), .clk(clk), .Q(Swait_q), .reset(reset_in));  // open: Qn, preset
  not not_1 (not_1_out, or_4_out);
  D_Flip_Flop Sload (.D(and_6_out), .clk(clk), .Q(mode0_out), .preset(1'b0), .reset(reset_in));  // open: Qn
  D_Flip_Flop Sshift (.D(or_3_out), .clk(clk), .Q(mode1_out), .preset(1'b0), .reset(reset_in));  // open: Qn
  D_Flip_Flop u_Swait_timer (.D(and_7_out), .clk(clk), .Q(Swait_timer), .preset(1'b0), .reset(reset_in));  // open: Qn
  not not_2 (Swait, Swait_q);
  or or_5 (tx_done_out, Swait, mode0_out);

  // Other names for the same wires on the sheet: done = done_in; m0_out = mode0_out; Sload = mode0_out;
  //   m1_out = mode1_out; Sshift = mode1_out; reset_t = reset_in; timer = timer_in; Tx_done_out_t = Swait

  // Notes on the sheet:
  //   Wait = 0001
  //   Attention, votre version de Logisim
  //   Load = 0010
  //   Shift = 0100
  //   ne contient pas de tracker. Si vous
  //   wait_timer = 1000
  //   enregistrez votre projet, toutes les
  //   informations du tracker seront
  //   définitivement effacées.
  //   Rising edge send
endmodule
